# Fritzing sketch snowdon (saved by Fritzing 0.9.3b)

parts:
  Part1 = Snowdon
  Mod1 = Raspberry Pi Pico W
  part = Resistor [tolerance=±5% resistance=220 package=THT]

nets:
  N1: Part1.pin0, Mod1.pin_25
  N2: Part1.pin_1, Mod1.pin_24
  N3: Part1.pin_2, Mod1.pin_22
  N4: Part1.pin_3, Mod1.pin_39
  N5: Part1.pin_4, part.Pin_0
  N6: Part1.pin_6, Mod1.pin_43
  N7: Part1.pin_7, Mod1.pin_41
  N8: Part1.pin_10, Part1.pin_11, Mod1.pin_38

custom parts:
  Raspberry Pi Pico W: Raspberry Pi Pico W. Based around the RP2040 microcontroller the Pico W is a low cost microcontroller device bringing Raspberry Pi quality, cost, and easy of use to the microcontroller space. The areas marked KEEPOUT in pcb silkscreen should not have traces running through them to avoid shorts on a soldered in module!
